# Fritzing sketch pdp7badge (saved by Fritzing 0.7.4b)
breadboards: 2

parts:
  DI1 = 7-Segment LED Display [package=THT]
  DI2 = 7-Segment LED Display [package=THT]
  DI3 = 7-Segment LED Display [package=THT]
  DI4 = 7-Segment LED Display [package=THT]
  R2 = Resistor [resistance=22 tolerance=±5% package=THT]
  Part1 = Arduino Pro Mini 3.3V
  S1 = Toggle Switch [package=THT]
  R5 = Rotary Potentiometer (Small) [maximum_resistance=100kΩ]
  R6 = Resistor [resistance=22 tolerance=±5% package=THT]
  R7 = Resistor [resistance=22 tolerance=±5% package=THT]
  R8 = Resistor [resistance=22 tolerance=±5% package=THT]
  LiPo = rounded female pin header, 2 pins [form="♀ (female rounded)"]

nets:
  N1: DI1.cathodeE, DI1.cathodeD, DI1.cathodeC, DI2.cathodeE, DI3.cathodeE, DI4.cathodeC, R5.leg2, LiPo.pin2
  N2: DI1.cathodeB, DI1.cathodeG, DI2.cathodeB, DI2.cathodeA, DI2.cathodeF, DI2.cathodeG, DI3.cathodeB, DI3.cathodeA, DI3.cathodeF, DI3.cathodeG, DI4.cathodeB, DI4.cathodeA
  N3: DI1.commAnode#7, R2.Pin_1
  N4: DI2.commAnode#7, R8.Pin_1
  N5: DI3.commAnode#7, R7.Pin_1
  N6: DI4.commAnode#7, R6.Pin_1
  N7: R2.Pin_0, Part1.D5
  N8: Part1.RAW, S1.L1
  N9: Part1.VCC, R5.leg1
  N10: Part1.A0, R5.wiper
  N11: Part1.D9, R6.Pin_0
  N12: Part1.D6, R7.Pin_0
  N13: Part1.D3, R8.Pin_0
  N14: S1.COM, LiPo.pin1

notes:
  SparkFun 3.7V 400mAh LiPo Battery
  to program, turn off battery & connect SparkFun 3.3V FTDI Basic Breakout
